// Logisim project 4bitrippleadder.circ as structural Verilog
module main (
  input  Ci,
  input  A0,
  input  A1,
  input  A2,
  input  A3,
  input  B0,
  input  B1,
  input  B2,
  input  B3
);

  wire and_1_out, and_2_out, and_3_out, and_4_out, and_5_out, and_6_out, and_7_out, and_8_out, C0_out,
       C1_out, C2_out, clock_1_out, Co_out, d_ff_1_q, d_ff_2_q, d_ff_3_q, d_ff_4_q, d_ff_5_q, S0_out, S1_out,
       S2_out, S3_out, xor_1_out, xor_2_out, xor_3_out, xor_4_out;

  ExactlyOne S0 (.out(S0_out), .in0(A0), .in1(B0), .in2(Ci));
  and and_1 (and_1_out, A0, B0);
  xor xor_1 (xor_1_out, A0, B0);
  ExactlyOne S1 (.out(S1_out), .in0(A1), .in1(B1), .in2(C0_out));
  and and_2 (and_2_out, A1, B1);
  xor xor_2 (xor_2_out, A1, B1);
  ExactlyOne S2 (.out(S2_out), .in0(B2), .in1(A2), .in2(C1_out));
  and and_3 (and_3_out, A2, B2);
  xor xor_3 (xor_3_out, A2, B2);
  ExactlyOne S3 (.out(S3_out), .in0(A3), .in1(B3), .in2(C2_out));
  and and_4 (and_4_out, B3, A3);
  xor xor_4 (xor_4_out, A3, B3);
  and and_5 (and_5_out, xor_2_out, C0_out);
  Clock clock_1 (.out(clock_1_out));
  and and_6 (and_6_out, xor_1_out, Ci);
  and and_7 (and_7_out, xor_3_out, C1_out);
  and and_8 (and_8_out, xor_4_out, C2_out);
  D_Flip_Flop d_ff_1 (.clk(clock_1_out), .D(S0_out), .Q(d_ff_1_q));  // open: Qn, preset, en, reset
  or C0 (C0_out, and_1_out, and_6_out);
  D_Flip_Flop d_ff_2 (.clk(clock_1_out), .D(S1_out), .Q(d_ff_2_q));  // open: Qn, preset, en, reset
  or C1 (C1_out, and_2_out, and_5_out);
  or C2 (C2_out, and_3_out, and_7_out);
  or Co (Co_out, and_4_out, and_8_out);
  LED led_1 (.in(d_ff_1_q));
  LED led_2 (.in(d_ff_2_q));
  D_Flip_Flop d_ff_3 (.clk(clock_1_out), .D(S2_out), .Q(d_ff_3_q));  // open: Qn, preset, en, reset
  D_Flip_Flop d_ff_4 (.clk(clock_1_out), .D(S3_out), .Q(d_ff_4_q));  // open: Qn, preset, en, reset
  LED led_3 (.in(d_ff_3_q));
  LED led_4 (.in(d_ff_4_q));
  D_Flip_Flop d_ff_5 (.clk(clock_1_out), .D(Co_out), .Q(d_ff_5_q));  // open: Qn, preset, en, reset
  LED led_5 (.in(d_ff_5_q));
endmodule
