// Logisim project ENCODER.circ as structural Verilog: 1 circuit, main circuit main
module main (
  input  I0,
  input  in_2,
  input  I2,
  input  in_4,
  input  in_5,
  input  I5,
  input  in_7,
  input  in_8
);

  wire D1_out, D2_out, D3_out;

  or D1 (D1_out, in_5, I5, in_7, in_8);
  or D2 (D2_out, in_2, in_4, in_7, in_8);
  or D3 (D3_out, in_2, in_4, I5, in_8);
  LED led_1 (.in(D1_out));
  LED led_2 (.in(D2_out));
  LED led_3 (.in(D3_out));

  // Notes on the sheet:
  //   I3
  //   I1
  //   I4
  //   I7
  //   I6
endmodule
