// Logisim project commonBus.circ as structural Verilog: 1 circuit, main circuit main
module main (
  input  [1:0] in_1,
  input  [3:0] in_2,
  input  [3:0] in_3,
  input  [3:0] in_4,
  input  [3:0] in_5,
  input  in_6,
  input  in_7,
  input  in_8,
  input  in_9,
  output [3:0] out_10
);

  wire clock_1_out;
  wire [3:0] register_1_q, register_2_q, register_3_q, register_4_q;

  Clock clock_1 (.out(clock_1_out));
  Register #(.width(4)) register_1 (.D(in_5), .en(in_9), .clk(clock_1_out), .Q(register_1_q));  // open: clr
  Multiplexer #(.select(2)) multiplexer_1 (
    .in0(register_1_q[0]), .in1(register_2_q[0]), .in2(register_3_q[0]), .in3(register_4_q[0]),
    .out(out_10[0]), .sel(in_1));
  Register #(.width(4)) register_2 (.D(in_2), .en(in_6), .clk(clock_1_out), .Q(register_2_q));  // open: clr
  Multiplexer #(.select(2)) multiplexer_2 (
    .in0(register_1_q[1]), .in1(register_2_q[1]), .in2(register_3_q[1]), .in3(register_4_q[1]),
    .out(out_10[1]), .sel(in_1));
  Register #(.width(4)) register_3 (.D(in_4), .en(in_8), .clk(clock_1_out), .Q(register_3_q));  // open: clr
  Multiplexer #(.select(2)) multiplexer_3 (
    .in0(register_1_q[2]), .in1(register_2_q[2]), .in2(register_3_q[2]), .in3(register_4_q[2]),
    .out(out_10[2]), .sel(in_1));
  Register #(.width(4)) register_4 (.D(in_3), .en(in_7), .clk(clock_1_out), .Q(register_4_q));  // open: clr
  Multiplexer #(.select(2)) multiplexer_4 (
    .in0(register_1_q[3]), .in1(register_2_q[3]), .in2(register_3_q[3]), .in3(register_4_q[3]),
    .out(out_10[3]), .sel(in_1));
endmodule
