// Logisim project multiplexer.circ as structural Verilog: 1 circuit, main circuit main
module main (
  input  in_1,
  input  in_2,
  input  in_3,
  input  in_4,
  input  in_5,
  input  in_6,
  input  in_7,
  input  in_8,
  input  in_9,
  input  in_10,
  input  in_11,
  input  in_12,
  input  in_13,
  input  in_14
);

  wire and_1_out, and_2_out, and_3_out, and_4_out, and_5_out, and_6_out, and_7_out, and_8_out, and_9_out,
       and_10_out, not_1_out, not_2_out, not_3_out, not_4_out, or_1_out, or_2_out;

  not not_1 (not_1_out, in_2);
  not not_2 (not_2_out, in_12);
  not not_3 (not_3_out, in_13);
  not not_4 (not_4_out, in_14);
  and and_1 (and_1_out, in_1, in_2);
  and and_2 (and_2_out, in_3, not_1_out);
  and and_3 (and_3_out, in_4, not_2_out, not_3_out, not_4_out);
  and and_4 (and_4_out, in_5, not_2_out, not_3_out, in_14);
  and and_5 (and_5_out, in_6, not_2_out, in_13, not_4_out);
  and and_6 (and_6_out, in_7, not_2_out, in_12, in_13);
  and and_7 (and_7_out, in_8, in_14, not_4_out, not_3_out);
  and and_8 (and_8_out, in_9, in_12, not_3_out, in_14);
  and and_9 (and_9_out, in_10, in_12, in_13, not_4_out);
  and and_10 (and_10_out, in_11, in_12, in_13, in_14);
  or or_1 (or_1_out, and_1_out, and_2_out);
  LED led_1 (.in(or_1_out));
  or or_2 (or_2_out, and_3_out, and_4_out, and_5_out, and_6_out, and_7_out, and_8_out, and_9_out, and_10_out);
  LED led_2 (.in(or_2_out));
endmodule
